// Logisim project Yashika_ALU.circ as structural Verilog: 9 circuits, main circuit  Main ALU Circuit
module _16_Bit_AND (
  input  [15:0] A,
  input  [15:0] B,
  output [15:0] C
);

  assign C = A & B;  // AND_Gate and_1, 16 bits wide

  // Notes on the sheet:
  //   16-Bit AND
  //   A= 110 b= 60  C=44(All values are in binary)
endmodule

module _16_Bit_OR (
  input  [15:0] A,
  input  [15:0] B,
  output [15:0] C
);

  assign C = A | B;  // OR_Gate or_1, 16 bits wide

  // Notes on the sheet:
  //   16-Bit OR
endmodule

module _16_Bit_XOR (
  input  [15:0] A,
  input  [15:0] B,
  output [15:0] C
);

  assign C = A ^ B;  // XOR_Gate xor_1, 16 bits wide

  // Notes on the sheet:
  //   16-bit XOR
endmodule

module _16_Bit_Inverter (
  input  [15:0] A,
  output [15:0] C
);

  assign C = ~A;  // NOT_Gate not_1, 16 bits wide

  // Notes on the sheet:
  //   16-Bit Inverter
endmodule

module _16_Bit_Adder (
  input  [15:0] A,
  input  [15:0] B,
  output [15:0] C,
  output [15:0] C_2
);

  wire adder_1_cout;
  wire [15:0] undriven;

  assign C = A & B;  // AND_Gate and_1, 16 bits wide
  Adder #(.width(16)) adder_1 (.a(undriven), .out(C_2), .cout(adder_1_cout));  // open: b, cin

  // Notes on the sheet:
  //   16-Bit Adder
  //   Please notice that you need to generate the four flag bits for the adder.
endmodule

module _16_Bit_Subtractor (
);


  // Notes on the sheet:
  //   16-Bit Subtractor
  //   Please notice that you need to generate the four flag bits for the subtractor
endmodule

module _16_Bit_Left_Shifter_Circuit (
  input  [15:0] A,
  input  [3:0] B,
  output [15:0] out_3
);

  Shifter #(.width(16)) shifter_1 (.in(A), .\dist (B), .out(out_3));

  // Notes on the sheet:
  //   Shift A to left by B bits
  //   16-Bit Left Shifter Circuit
endmodule

module _16_Bit_Right_Shfit_Circuit (
  input  [15:0] A,
  input  [3:0] B,
  output [15:0] out_3
);

  Shifter #(.width(16), .shift("lr")) shifter_1 (.in(A), .\dist (B), .out(out_3));

  // Notes on the sheet:
  //   Shift A to Right by B bits
  //   16-Bit Right Shifter Circuit
endmodule

module Main_ALU_Circuit (
);


  // Notes on the sheet:
  //   Main ALU Circuit to Build
  //   Needs to use all the subcircuits you built
endmodule
